# Fritzing sketch relay (saved by Fritzing 0.9.6b)
breadboards: 1

parts:
  U8 = RELAY [part_number=15A package=relay-t9a-2]
  Q5 = NPN-Transistor [package="TO92 [THT]"]
  D4 = Rectifier Diode [part_number=1N4001 package="300 mil [THT]"]
  U9 = Optocoupler [package=THT]
  LED2 = LED - 5mm [color="Red (633nm)" current=0.030 package="5 mm [THT]"]
  R25 = Resistor [tolerance=±5% power=0.25 resistance=510 package=THT]
  R26 = Resistor [tolerance=±5% power=0.25 resistance=1k package=THT]

nets:
  5V: U8.COIL1, D4.cathode, U9.Pin_5, R26.Pin_0
  N1: U8.COIL2, Q5.C, D4.anode
  GND: Q5.E
  N2: Q5.B, R25.Pin_0
  N3: U9.Pin_1, R26.Pin_1
  N4: U9.Pin_2, LED2.anode
  N5: U9.Pin_4, R25.Pin_1
